# Fritzing sketch fake-eastron-and-modbus-bridge (saved by Fritzing 0.9.5d)
circuit board: 8.46667cm x 5.64444cm

parts:
  A1 = Esp32-c3 super mini
  U3 = Mini-360 DC-DC Buck converter [package=THT]
  M1 = MAX485 Breakout [package=THT]
  M2 = MAX485 Breakout [package=THT]
  A2 = Current transformer PZCT02
  A3 = Current transformer PZCT02
  A4 = Current transformer PZCT02
  R1 = Resistor [tolerance=±0.5% resistance=50 package=THT]
  R2 = Resistor [tolerance=±0.5% resistance=50 package=THT]
  R3 = Resistor [tolerance=±0.5% resistance=50 package=THT]
  M3 = MAX485 Breakout [package=THT]
  R5 = Resistor [tolerance=±0.5% resistance=1200 package=THT]
  R6 = Resistor [tolerance=±0.5% resistance=330 package=THT]

nets:
  N1: A1.Pin_1, M2.DI
  N2: A1.Pin_2, M2.RO
  N3: A1.Pin_3, M3.DI
  N4: A1.Pin_5, M3.RO
  N5: A1.Pin_7, M1.DI
  N6: A1.Pin_8, M1.RO
  N7: A1.Pin_9, A3.Pin_2, R1.Pin_1
  N8: A1.Pin_10, A2.Pin_2, R2.Pin_1
  N9: A1.Pin_11, A4.Pin_2, R3.Pin_1
  N10: A1.Pin_15, U3.OUT-, R6.Pin_0
  N11: A1.Pin_16, U3.OUT+
  VCC: M1.VCC, M2.VCC, M3.VCC
  N12: A2.Pin_1, R2.Pin_0
  N13: A3.Pin_1, R1.Pin_0
  N14: A4.Pin_1, R3.Pin_0, R5.Pin_0

notes:
  Deye ModeBUS port for
  Solarman integration
  Colors with RJ45 568A plug
  Deye (external) Meter-485 port
  Colors with RJ45 586A plug
  Deye BMS port (RS485 wires)
  CAN uses middle wires (blue)
  Split core current transformers
  with 3000:1 ratio or less
  Pin7 (+) of Deye CN2 (RST port)
  Pin 8 (-) of Deye CN2

custom parts:
  Esp32-c3 super mini: ESP32-C3 Development Board ESP32 SuperMini Development Board ESP32 Development Board WiFi Bluetooth.
  Mini-360 DC-DC Buck converter: Mini-360 DC-DC Buck converter. Tiny buck step down voltage converter, input voltage 4.75 to 23V output 1 to 17V adjustable. Available from ebay and the like.
  MAX485 Breakout: MAX485 RS485 breakout board
  Current transformer PZCT02: Current transformer PZCT02.
